# Fritzing sketch Stepper with Blynk (saved by Fritzing 0.9.3b)
circuit board: 8.46667cm x 5.64444cm
breadboards: 1

parts:
  U1 = NodeMCU V1.0
  MOTOR1 = 28BYJ-48 Stepper Motor
  BREAKOUT1 = ULN2003A breakout board
  HLK-PM1 = HLK-PM01

nets:
  N1: U1.D1, BREAKOUT1.In_1
  N2: U1.D2, BREAKOUT1.In_3
  N3: U1.D3, BREAKOUT1.In_2
  N4: U1.D4, BREAKOUT1.In_4
  N5: MOTOR1.RED, BREAKOUT1.RED_wire
  N6: MOTOR1.ORANGE, BREAKOUT1.ORANGE_wire
  N7: MOTOR1.YELLOW, BREAKOUT1.YELLOW_wire
  N8: MOTOR1.PINK, BREAKOUT1.PINK_wire
  N9: MOTOR1.BLUE, BREAKOUT1.BLUE_wire
  N10: BREAKOUT1.0V, HLK-PM1.-Vo
  N11: BREAKOUT1.+5V, HLK-PM1.+Vo

custom parts:
  NodeMCU V1.0: ESP8266 based NodeMCU
  ULN2003A breakout board: ULN2003A 7-way Darlington Transistor Driver on breakoutboard

// code stored in the sketch: Code.ino
#include <Blynk.h>

/********************************************************************************************
*Project:              Stepper motor control with Blynk App                                 *
*Author:               Epic Electronics                                                     *
*Youtube channel:      https://www.youtube.com/channel/UCUvW5tOMS4KRXxMFt33XYvg/featured    *
*Programming Date:     10.02.2020                                                           *
*Version:              V3.3                                                                 *
*Last Update:          12.04.2020                                                           *
*Video from project:   https://youtu.be/elKlWb9ru5o                                         *
*                                                                                           *
*About:   The program reads the actual state from the blynk app and controls a steppermotor.*
*         If the button on the blynk app is trigged, the steppermotor rotats in the given   *
*         direction 10 times for 360 degree, total 3600 degree.                             *
********************************************************************************************/

#include <Stepper.h>
#include <ESP8266WiFi.h>
#include <WiFiClient.h>;
#include <BlynkSimpleEsp8266.h>

#define BLYNK_PRINT Serial

const int stepsPerRevolution = 200;
Stepper my_Stepper(stepsPerRevolution, 5, 4, 0, 2);

bool Right = false;
bool Left = false;

char auth[] = "qyjcjS2b8hsRu4ucVuG8yUPF4WxKVCM3";
char ssid[] = "GEARBOX STAFF";
char pass[] = "Staff@Gearbox";


//++ Start Setup +++++++++++++++++++++++++++++++++++++++++++++++++++++++++++++++++++++++++++++++++++++++++++++++++++++++++++++++++++
void setup(){

  Serial.begin(9600);                                 // baudrate for serial comunication
   WiFi.begin(ssid, pass);
  Blynk.begin(auth, ssid, pass);                      // network information 
  my_Stepper.setSpeed(70);                            // Speed for stepper motor
  
}
//-- Setup End ---------------------------------------------------------------------------------------------------------------------


BLYNK_WRITE(V1){                                      // read input from virtual pin V1
  Right = param.asInt();                              // assigning incoming value from pin V1 to a variable
  }
  
BLYNK_WRITE(V0){                                      // read input from virtual pin V0
  Left = param.asInt();                               // assigning incoming value from pin V0 to a variable
  }
  
void Stepper1 (int Direction, int Rotation){          // function for stepper motor control with 2 parameters
  for (int i = 0; i < Rotation; i++){                 // for loop 
  my_Stepper.step(Direction * 100);                   // 200 is 360 degree => change value if smaller then 360 degree is needing
  Blynk.run();
  }
}

//++ Start Loop +++++++++++++++++++++++++++++++++++++++++++++++++++++++++++++++++++++++++++++++++++++++++++++++++++++++++++++++++++
void loop() {   
  
  Blynk.run();
  
  if (Right){                                          // if condition 
  Stepper1(1, 1);                                     // steppermotor rotates 1 times 360 degree right
  Serial.println("Clockwise");
  }
  delay(20);                                           // delay 20ms
  
  if (Left){                                           // if condition 
  Stepper1(-1, 1);                                    // steppermotor rotates 1 times 360 degree left
  Serial.println("Anticlockwise");
  }
  delay(20);                                           // delay 20ms
}
//-- Loop End ---------------------------------------------------------------------------------------------------------------------
