# Fritzing sketch Stepper with Blynk (saved by Fritzing 0.9.3b)
circuit board: 8.46667cm x 5.64444cm
breadboards: 1

parts:
  U1 = NodeMCU V1.0
  MOTOR1 = 28BYJ-48 Stepper Motor
  BREAKOUT1 = ULN2003A breakout board
  HLK-PM1 = HLK-PM01

nets:
  N1: U1.D1, BREAKOUT1.In_1
  N2: U1.D2, BREAKOUT1.In_3
  N3: U1.D3, BREAKOUT1.In_2
  N4: U1.D4, BREAKOUT1.In_4
  N5: MOTOR1.RED, BREAKOUT1.RED_wire
  N6: MOTOR1.ORANGE, BREAKOUT1.ORANGE_wire
  N7: MOTOR1.YELLOW, BREAKOUT1.YELLOW_wire
  N8: MOTOR1.PINK, BREAKOUT1.PINK_wire
  N9: MOTOR1.BLUE, BREAKOUT1.BLUE_wire
  N10: BREAKOUT1.0V, HLK-PM1.-Vo
  N11: BREAKOUT1.+5V, HLK-PM1.+Vo

custom parts:
  NodeMCU V1.0: ESP8266 based NodeMCU
  ULN2003A breakout board: ULN2003A 7-way Darlington Transistor Driver on breakoutboard
